# Fritzing sketch FalconRC 4X Sketch (saved by Fritzing 0.9.2b)
breadboards: 1

parts:
  Part1 = Arduino Nano (Rev3.0)
  Part2 = Thumb Joystick
  NRF24L01 = NRF24L01
  Part3 = Thumb Joystick
  R1 = Resistor [tolerance=±5% resistance=220 package="2512 [SMD]"]
  R2 = Resistor [tolerance=±5% resistance=220 package="2512 [SMD]"]
  R3 = Resistor [tolerance=±5% resistance=220 package="2512 [SMD]"]
  R4 = Resistor [tolerance=±5% resistance=220 package="2512 [SMD]"]
  C1 = Ceramic Capacitor [capacitance=100nF package="100 mil [THT, multilayer]"]
  C2 = Ceramic Capacitor [capacitance=100nF package="100 mil [THT, multilayer]"]
  C3 = Ceramic Capacitor [capacitance=100nF package="100 mil [THT, multilayer]"]
  C4 = Ceramic Capacitor [capacitance=100nF package="100 mil [THT, multilayer]"]
  LED1 = LED - 5mm [color="Red (633nm)" package="5 mm [THT]"]
  R5 = Resistor [tolerance=±5% resistance=220 package=THT]
  C5 = Tantalum Capacitor [capacitance=10µF package="100 mil [THT, tantalum]"]
  C6 = Ceramic Capacitor [capacitance=100nF package="100 mil [THT, multilayer]"]
  VCC1 = Battery block 9V
  S1 = SPST Switch [package=switch-spdt]
  R6 = Resistor [tolerance=±5% resistance=10k package=THT]
  R7 = Resistor [tolerance=±5% resistance=2.2k package=THT]
  C7 = Ceramic Capacitor [capacitance=100nF package="100 mil [THT, multilayer]"]

nets:
  GND: Part1.GND, Part2.GND, Part3.GND, C1.0, C2.0, C3.0, C4.0, LED1.cathode, VCC1.-
  N1: Part1.D3, R5.Pin_0
  N2: Part1.D9, NRF24L01.CE
  N3: Part1.D10, NRF24L01.CSN
  N4: Part1.D11/MOSI, NRF24L01.MOSI
  N5: Part1.D12/MISO, NRF24L01.MISO
  N6: Part1.VIN, S1.S, R6.Pin_0
  VCC: Part1.5V, Part2.VCC, Part3.VCC
  N7: Part1.A4, R6.Pin_1, R7.Pin_0, C7.0
  N8: Part1.A3, R4.Pin_1, C1.1
  N9: Part1.A2, R3.Pin_1, C2.1
  N10: Part1.A1, R2.Pin_1, C3.1
  N11: Part1.A0, R1.Pin_1, C4.1
  3V3: Part1.3V3, NRF24L01.VCC, C5.+, C6.1
  N12: Part1.D13/SCK, NRF24L01.SCK
  N13: Part2.HORZ, R1.Pin_0
  N14: Part2.VERT, R2.Pin_0
  N15: NRF24L01.GND, C5.-, C6.0, R7.Pin_1, C7.1
  N16: Part3.HORZ, R3.Pin_0
  N17: Part3.VERT, R4.Pin_0
  N18: LED1.anode, R5.Pin_1
  N19: VCC1.+, S1.P

custom parts:
  NRF24L01: NRF24L01 module
